# Fritzing sketch printpy (saved by Fritzing 1.0.0d)

parts:
  S1 = Pushbutton [package="[THT]"]
  J3 = female pin header, 2 pins [form="♀ (female)"]
  J4 = female pin header, 2 pins [form="♀ (female)"]
  J5 = female pin header, 2 pins [form="♀ (female)"]
  OLED1 = OLED 128x64 I2C Monochrome Display GND-VDD
  OLED2 = OLED 128x64 I2C Monochrome Display GND-VDD
  Mod1 = seeeduino-xiao

nets:
  N1: S1.Pin_3, S1.Pin_4, Mod1.D8
  N2: J3.pin1, Mod1.D6
  N3: J4.pin1, Mod1.5V
  N4: J5.pin2, Mod1.D7
  VDD: OLED1.VDD, Mod1.3V3
  N5: OLED1.SCK, Mod1.D3
  N6: OLED1.SDA, Mod1.D2
  N7: OLED2.SCK, Mod1.D5
  N8: OLED2.SDA, Mod1.D4

notes:
  5v
  RX
  GND
  TX
  Duet/RRF
  UART port
  3v3
  3V3
  5V
  PrintPY
  easytarget/
  2040
  XIAO
  2xOLED I2C
  Button
  Alternate: Single I2C port:
  I2C address jumpers on one OLED
  and wiring SDA/SCK in parallel
  I2C1
  I2C0
  Share the I2C bus by
  changing
  By Owen
  github.com/
  PrintPy2040
  https://
  <==>
  PrintPy2040 hookup guide:
  - Suitable for 'rats nest' free-form wiring.
  - If using supplied case *do not* solder pinheaders to OLED or XIAO boards.

custom parts:
  OLED 128x64 I2C Monochrome Display GND-VDD: OLED 128x64 I2C Monochrome Display. Note: there are two variants of this part, this one is the GND VDD SCK SDA variant. The other is VDD GND SCK SDA. Make sure you select the part that matches your module as using the incorrect part will probably destroy your module! In addition the mounting holes are marked on silkscreen but not by default drilled. If you want drilled mounting holes, copy a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
  seeeduino-xiao: Seeeduino XIAO processor board.
